# Fritzing sketch Untitled Sketch 2 (saved by Fritzing 0.9.0b)
circuit board: 8.46667cm x 5.64444cm
breadboards: 1

parts:
  IC1 = OP482 - Low Power, High Speed JFET Quad Operational Amplifier [part_number=NTE987]
  R2 = Resistor [tolerance=±5% resistance=4.7 package=THT]
  R3 = Resistor [tolerance=±5% resistance=4.7 package=THT]
  R4 = Resistor [tolerance=±5% resistance=4.7 package=THT]
  R5 = Resistor [tolerance=±5% resistance=10k package=THT]
  R6 = Resistor [tolerance=±5% resistance=10k package=THT]
  R7 = Resistor [tolerance=±5% resistance=10k package=THT]
  R8 = Resistor [tolerance=±5% resistance=10k package=THT]
  Q1 = Basic FET N-Channel [package="TO220 [THT]"]
  Q3 = Basic FET N-Channel [package="TO220 [THT]"]
  Q4 = Basic FET N-Channel [package="TO220 [THT]"]
  LED1 = LED - 5mm [color="Red (633nm)" package="5 mm [THT]"]
  LED2 = LED - 5mm [color="Red (633nm)" package="5 mm [THT]"]
  LED3 = LED - 5mm [color="Red (633nm)" package="5 mm [THT]"]
  LED4 = LED - 5mm [color="Red (633nm)" package="5 mm [THT]"]
  R10 = Resistor [tolerance=±5% resistance=1k package=THT]
  R11 = Resistor [tolerance=±5% resistance=1k package=THT]
  R12 = Resistor [tolerance=±5% resistance=1k package=THT]
  C1 = Ceramic Capacitor [capacitance=10nF voltage=50V package="200 mil [THT, multilayer]"]
  R1 = Resistor [tolerance=±5% resistance=4.7 package=THT]
  R13 = Resistor [tolerance=±5% resistance=1k package=THT]
  J1 = female pin header, 6 pins [form="♀ (female)"]
  Q2 = Basic FET N-Channel [package="TO220 [THT]"]

nets:
  N1: IC1.OUTA, Q4.gate
  N2: IC1.-INA, R2.Pin_1, Q4.source
  N3: IC1.+INA, R8.Pin_0, R11.Pin_0
  5V: IC1.V+, LED1.anode, LED2.anode, LED3.anode, LED4.anode, C1.1, J1.pin1
  N4: IC1.+INB, R7.Pin_0, R12.Pin_0
  N5: IC1.-INB, R4.Pin_1, Q1.source
  N6: IC1.OUTB, Q1.gate
  N7: IC1.OUTC, Q2.gate
  N8: IC1.-INC, R3.Pin_1, Q2.source
  N9: IC1.+INC, R6.Pin_1, R13.Pin_1
  GND: IC1.V-, R2.Pin_0, R3.Pin_0, R4.Pin_0, R10.Pin_1, R11.Pin_1, R12.Pin_1, C1.0, R1.Pin_0, R13.Pin_0, J1.pin6
  N10: IC1.+IND, R5.Pin_1, R10.Pin_0
  N11: IC1.-IND, Q3.source, R1.Pin_1
  N12: IC1.OUTD, Q3.gate
  N13: R5.Pin_0, J1.pin2
  N14: R6.Pin_0, J1.pin5
  N15: R7.Pin_1, J1.pin4
  N16: R8.Pin_1, J1.pin3
  N17: Q1.drain, LED3.cathode
  N18: Q3.drain, LED1.cathode
  N19: Q4.drain, LED2.cathode
  N20: LED4.cathode, Q2.drain

notes:
  Keep C1 as close
  to IC1 as possible

custom parts:
  OP482 - Low Power, High Speed JFET Quad Operational Amplifier: Quad Op Amp
